// Logisim project Elevator.circ as structural Verilog: 7 circuits, main circuit Ascensore
module Piano_1 (
  input  in_1,
  output [6:0] out_2,
  output [6:0] out_3,
  output [6:0] out_4,
  output [6:0] out_5,
  output [6:0] out_6,
  output [6:0] out_7,
  output [6:0] out_8,
  output [6:0] out_9
);

  Multiplexer #(.width(7)) multiplexer_1 (.in0({7{1'b0}}), .in1(7'b0000100), .out(out_2), .sel(in_1));  // open: en
  Multiplexer #(.width(7)) multiplexer_2 (.in0({7{1'b0}}), .in1(7'b0001001), .out(out_3), .sel(in_1));  // open: en
  Multiplexer #(.width(7)) multiplexer_3 (.in0({7{1'b0}}), .in1(7'b0010001), .out(out_4), .sel(in_1));  // open: en
  Multiplexer #(.width(7)) multiplexer_4 (.in0({7{1'b0}}), .in1(7'b0111111), .out(out_5), .sel(in_1));  // open: en
  Multiplexer #(.width(7)) multiplexer_5 (.in0({7{1'b0}}), .in1(7'b0000001), .out(out_6), .sel(in_1));  // open: en
  Multiplexer #(.width(7)) multiplexer_6 (.in0({7{1'b0}}), .in1(7'b0000001), .out(out_7), .sel(in_1));  // open: en
  Multiplexer #(.width(7)) multiplexer_7 (.in0({7{1'b0}}), .in1({7{1'b0}}), .out(out_8), .sel(in_1));  // open: en

  assign out_9 = {{5{1'b0}}, in_1, 1'b0};
endmodule

module Piano_2 (
  input  in_1,
  output [6:0] out_2,
  output [6:0] out_3,
  output [6:0] out_4,
  output [6:0] out_5,
  output [6:0] out_6,
  output [6:0] out_7,
  output [6:0] out_8,
  output [6:0] out_9
);

  Multiplexer #(.width(7)) multiplexer_1 (.in0({7{1'b0}}), .in1({7{1'b0}}), .out(out_2), .sel(in_1));  // open: en
  Multiplexer #(.width(7)) multiplexer_2 (.in0({7{1'b0}}), .in1(7'b0010011), .out(out_3), .sel(in_1));  // open: en
  Multiplexer #(.width(7)) multiplexer_3 (.in0({7{1'b0}}), .in1(7'b0100101), .out(out_4), .sel(in_1));  // open: en
  Multiplexer #(.width(7)) multiplexer_4 (.in0({7{1'b0}}), .in1(7'b0101001), .out(out_5), .sel(in_1));  // open: en
  Multiplexer #(.width(7)) multiplexer_5 (.in0({7{1'b0}}), .in1(7'b0010001), .out(out_6), .sel(in_1));  // open: en
  Multiplexer #(.width(7)) multiplexer_6 (.in0({7{1'b0}}), .in1(7'b0000001), .out(out_7), .sel(in_1));  // open: en
  Multiplexer #(.width(7)) multiplexer_7 (.in0({7{1'b0}}), .in1({7{1'b0}}), .out(out_8), .sel(in_1));  // open: en

  assign out_9 = {4'b0000, in_1, 2'b00};
endmodule

module Piano_3 (
  input  in_1,
  output [6:0] out_2,
  output [6:0] out_3,
  output [6:0] out_4,
  output [6:0] out_5,
  output [6:0] out_6,
  output [6:0] out_7,
  output [6:0] out_8,
  output [6:0] out_9
);

  Multiplexer #(.width(7)) multiplexer_1 (.in0({7{1'b0}}), .in1({7{1'b0}}), .out(out_2), .sel(in_1));  // open: en
  Multiplexer #(.width(7)) multiplexer_2 (.in0({7{1'b0}}), .in1({7{1'b0}}), .out(out_3), .sel(in_1));  // open: en
  Multiplexer #(.width(7)) multiplexer_3 (.in0({7{1'b0}}), .in1(7'b0010101), .out(out_4), .sel(in_1));  // open: en
  Multiplexer #(.width(7)) multiplexer_4 (.in0({7{1'b0}}), .in1(7'b0010101), .out(out_5), .sel(in_1));  // open: en
  Multiplexer #(.width(7)) multiplexer_5 (.in0({7{1'b0}}), .in1(7'b0010101), .out(out_6), .sel(in_1));  // open: en
  Multiplexer #(.width(7)) multiplexer_6 (.in0({7{1'b0}}), .in1(7'b0011111), .out(out_7), .sel(in_1));  // open: en
  Multiplexer #(.width(7)) multiplexer_7 (.in0({7{1'b0}}), .in1({7{1'b0}}), .out(out_8), .sel(in_1));  // open: en

  assign out_9 = {3'b000, in_1, 3'b000};
endmodule

module Piano_terra (
  input  in_1,
  output [6:0] out_2,
  output [6:0] out_3,
  output [6:0] out_4,
  output [6:0] out_5,
  output [6:0] out_6,
  output [6:0] out_7,
  output [6:0] out_8,
  output [6:0] out_9
);

  Multiplexer #(.width(7)) multiplexer_1 (.in0({7{1'b0}}), .in1({7{1'b0}}), .out(out_2), .sel(in_1));  // open: en
  Multiplexer #(.width(7)) multiplexer_2 (.in0({7{1'b0}}), .in1(7'b0010000), .out(out_3), .sel(in_1));  // open: en
  Multiplexer #(.width(7)) multiplexer_3 (.in0({7{1'b0}}), .in1(7'b0010000), .out(out_4), .sel(in_1));  // open: en
  Multiplexer #(.width(7)) multiplexer_4 (.in0({7{1'b0}}), .in1(7'b0011111), .out(out_5), .sel(in_1));  // open: en
  Multiplexer #(.width(7)) multiplexer_5 (.in0({7{1'b0}}), .in1(7'b0010000), .out(out_6), .sel(in_1));  // open: en
  Multiplexer #(.width(7)) multiplexer_6 (.in0({7{1'b0}}), .in1(7'b0010000), .out(out_7), .sel(in_1));  // open: en
  Multiplexer #(.width(7)) multiplexer_7 (.in0({7{1'b0}}), .in1({7{1'b0}}), .out(out_8), .sel(in_1));  // open: en

  assign out_9 = {{6{1'b0}}, in_1};
endmodule

module Ascensore (
  input  Allarme,
  input  [2:0] N_persone
);

  wire _1_out, _2_out, _3_out, Allarme_t, and_5_out, and_6_out, and_7_out, and_8_out, and_9_out, and_10_out,
       and_11_out, and_12_out, and_13_out, and_14_out, clk, counter_1_carry, counter_2_carry, counter_4_q,
       counter_5_q, counter_6_q, decoder_1_out1, decoder_1_out2, decoder_1_out4, decoder_1_out8,
       n_persone_1_errore, OFF, off_out, ON, on_out, or_1_out, or_2_out, or_3_out, pause, T_out;
  wire [1:0] counter_3_q;
  wire [2:0] and_1_out, and_2_out;
  wire [3:0] counter_7_carry;
  wire [6:0] errore_limite_superato_1_out_2, errore_limite_superato_1_out_3, errore_limite_superato_1_out_4,
       errore_limite_superato_1_out_5, errore_limite_superato_1_out_6, errore_limite_superato_1_out_7,
       errore_limite_superato_1_out_8, errore_limite_superato_1_out_9, errore_limite_superato_1_out_10,
       errore_limite_superato_1_out_11, errore_limite_superato_1_out_12, errore_limite_superato_1_out_13,
       errore_limite_superato_1_out_14, errore_limite_superato_1_out_15, errore_limite_superato_1_out_16,
       errore_limite_superato_1_out_17, errore_limite_superato_1_out_18, errore_limite_superato_1_out_19,
       errore_limite_superato_1_out_20, errore_limite_superato_1_out_21, errore_limite_superato_1_out_22,
       multiplexer_1_out, piano_1_1_out_2, piano_1_1_out_3, piano_1_1_out_4, piano_1_1_out_5,
       piano_1_1_out_6, piano_1_1_out_7, piano_1_1_out_8, piano_1_1_out_9, piano_2_1_out_2, piano_2_1_out_3,
       piano_2_1_out_4, piano_2_1_out_5, piano_2_1_out_6, piano_2_1_out_7, piano_2_1_out_8, piano_2_1_out_9,
       piano_3_1_out_2, piano_3_1_out_3, piano_3_1_out_4, piano_3_1_out_5, piano_3_1_out_6, piano_3_1_out_7,
       piano_3_1_out_8, piano_3_1_out_9, piano_terra_1_out_2, piano_terra_1_out_3, piano_terra_1_out_4,
       piano_terra_1_out_5, piano_terra_1_out_6, piano_terra_1_out_7, piano_terra_1_out_8,
       piano_terra_1_out_9;

  Clock clock_1 (.out(clk));
  Button u_on (.out(on_out));
  Button u_off (.out(off_out));
  Counter #(.width(1), .max('h1)) counter_1 (
    .count(on_out), .carry(counter_1_carry), .clk(clk));  // open: load, D, Q, clr
  Counter #(.width(1), .max('h1)) counter_2 (
    .count(off_out), .carry(counter_2_carry), .clk(clk));  // open: load, D, Q, clr
  assign and_1_out = N_persone & {3{Allarme_t}};  // AND_Gate and_1, 3 bits wide
  Button _3 (.out(_3_out));
  Button _2 (.out(_2_out));
  Button _1 (.out(_1_out));
  Button T (.out(T_out));
  and and_2 (and_2_out[0], and_1_out[0], ON);
  and and_3 (and_2_out[1], and_1_out[1], ON);
  and and_4 (and_2_out[2], and_1_out[2], ON);
  and and_5 (and_5_out, ON, pause, Allarme_t, _3_out);
  and and_6 (and_6_out, ON, pause, Allarme_t, _2_out);
  and and_7 (and_7_out, ON, pause, Allarme_t, _1_out);
  and and_8 (and_8_out, ON, pause, Allarme_t, T_out);
  xor xor_1 (ON, counter_2_carry, counter_1_carry);
  xnor xnor_1 (OFF, counter_1_carry, counter_2_carry);
  Counter #(.width(2), .max('h3), .ongoal("load")) counter_3 (
    .count(ON), .Q(counter_3_q), .clk(clk), .clr(or_1_out));  // open: load, D, carry
  Counter #(.width(1), .max('h1)) counter_4 (
    .count(and_5_out), .Q(counter_4_q), .carry(counter_7_carry[3]), .clk(clk), .clr(or_1_out));  // open: load, D
  Counter #(.width(1), .max('h1)) counter_5 (
    .count(and_6_out), .Q(counter_5_q), .carry(counter_7_carry[2]), .clk(clk), .clr(or_1_out));  // open: load, D
  Counter #(.width(1), .max('h1)) counter_6 (
    .count(and_7_out), .Q(counter_6_q), .carry(counter_7_carry[1]), .clk(clk), .clr(or_1_out));  // open: load, D
  Counter #(.width(1), .max('h1)) counter_7 (
    .count(and_8_out), .carry(counter_7_carry[0]), .clk(clk), .clr(or_1_out));  // open: load, D, Q
  Hex_Digit_Display hex_digit_display_1 (.value({1'b0, and_2_out}));  // open: dp
  or or_1 (or_1_out, OFF, and_9_out, and_11_out, and_10_out, and_13_out, and_12_out, and_14_out);
  N_persone n_persone_1 (.N_persone_input(and_2_out), .Errore(n_persone_1_errore));
  and and_9 (and_9_out, counter_7_carry[0], counter_6_q);
  or or_2 (or_2_out, Allarme, n_persone_1_errore);
  and and_10 (and_10_out, counter_7_carry[0], counter_4_q);
  and and_11 (and_11_out, counter_7_carry[0], counter_5_q);
  xnor xnor_2 (Allarme_t, 1'b0, Allarme);
  or or_3 (or_3_out, Allarme, or_2_out, n_persone_1_errore);
  xnor xnor_3 (pause, n_persone_1_errore, 1'b0);
  and and_12 (and_12_out, counter_7_carry[1], counter_4_q);
  and and_13 (and_13_out, counter_7_carry[1], counter_5_q);
  DotMatrix #(.matrixcols(7)) dotmatrix_1 (
    .col0(errore_limite_superato_1_out_2), .col1(errore_limite_superato_1_out_3),
    .col2(errore_limite_superato_1_out_4), .col3(errore_limite_superato_1_out_5),
    .col4(errore_limite_superato_1_out_6), .col5(errore_limite_superato_1_out_7),
    .col6(errore_limite_superato_1_out_8));
  DotMatrix #(.matrixcols(7)) dotmatrix_2 (
    .col0(errore_limite_superato_1_out_9), .col1(errore_limite_superato_1_out_10),
    .col2(errore_limite_superato_1_out_11), .col3(errore_limite_superato_1_out_12),
    .col4(errore_limite_superato_1_out_13), .col5(errore_limite_superato_1_out_14),
    .col6(errore_limite_superato_1_out_15));
  Errore_limite_superato errore_limite_superato_1 (
    .in_1(or_3_out), .out_2(errore_limite_superato_1_out_2), .out_3(errore_limite_superato_1_out_3),
    .out_4(errore_limite_superato_1_out_4), .out_5(errore_limite_superato_1_out_5),
    .out_6(errore_limite_superato_1_out_6), .out_7(errore_limite_superato_1_out_7),
    .out_8(errore_limite_superato_1_out_8), .out_9(errore_limite_superato_1_out_9),
    .out_10(errore_limite_superato_1_out_10), .out_11(errore_limite_superato_1_out_11),
    .out_12(errore_limite_superato_1_out_12), .out_13(errore_limite_superato_1_out_13),
    .out_14(errore_limite_superato_1_out_14), .out_15(errore_limite_superato_1_out_15),
    .out_16(errore_limite_superato_1_out_16), .out_17(errore_limite_superato_1_out_17),
    .out_18(errore_limite_superato_1_out_18), .out_19(errore_limite_superato_1_out_19),
    .out_20(errore_limite_superato_1_out_20), .out_21(errore_limite_superato_1_out_21),
    .out_22(errore_limite_superato_1_out_22));
  and and_14 (and_14_out, counter_7_carry[2], counter_4_q);
  DotMatrix #(.matrixcols(7)) dotmatrix_3 (
    .col0(errore_limite_superato_1_out_16), .col1(errore_limite_superato_1_out_17),
    .col2(errore_limite_superato_1_out_18), .col3(errore_limite_superato_1_out_19),
    .col4(errore_limite_superato_1_out_20), .col5(errore_limite_superato_1_out_21),
    .col6(errore_limite_superato_1_out_22));
  Decoder #(.select(4)) decoder_1 (
    .out1(decoder_1_out1), .out2(decoder_1_out2), .out4(decoder_1_out4), .out8(decoder_1_out8),
    .sel(counter_7_carry));  // open: out0, out3, out5, out6, out7, out9, out10, out11, out12, out13, out14, out15, en
  DotMatrix #(.matrixcols(7)) dotmatrix_4 (
    .col0(piano_3_1_out_2), .col1(piano_3_1_out_3), .col2(piano_3_1_out_4), .col3(piano_3_1_out_5),
    .col4(piano_3_1_out_6), .col5(piano_3_1_out_7), .col6(piano_3_1_out_8));
  DotMatrix #(.matrixcols(7)) dotmatrix_5 (
    .col0(piano_2_1_out_2), .col1(piano_2_1_out_3), .col2(piano_2_1_out_4), .col3(piano_2_1_out_5),
    .col4(piano_2_1_out_6), .col5(piano_2_1_out_7), .col6(piano_2_1_out_8));
  DotMatrix #(.matrixcols(7)) dotmatrix_6 (
    .col0(piano_1_1_out_2), .col1(piano_1_1_out_3), .col2(piano_1_1_out_4), .col3(piano_1_1_out_5),
    .col4(piano_1_1_out_6), .col5(piano_1_1_out_7), .col6(piano_1_1_out_8));
  DotMatrix #(.matrixcols(7)) dotmatrix_7 (
    .col0(piano_terra_1_out_2), .col1(piano_terra_1_out_3), .col2(piano_terra_1_out_4),
    .col3(piano_terra_1_out_5), .col4(piano_terra_1_out_6), .col5(piano_terra_1_out_7),
    .col6(piano_terra_1_out_8));
  Piano_3 piano_3_1 (
    .in_1(decoder_1_out8), .out_2(piano_3_1_out_2), .out_3(piano_3_1_out_3), .out_4(piano_3_1_out_4),
    .out_5(piano_3_1_out_5), .out_6(piano_3_1_out_6), .out_7(piano_3_1_out_7), .out_8(piano_3_1_out_8),
    .out_9(piano_3_1_out_9));
  Piano_2 piano_2_1 (
    .in_1(decoder_1_out4), .out_2(piano_2_1_out_2), .out_3(piano_2_1_out_3), .out_4(piano_2_1_out_4),
    .out_5(piano_2_1_out_5), .out_6(piano_2_1_out_6), .out_7(piano_2_1_out_7), .out_8(piano_2_1_out_8),
    .out_9(piano_2_1_out_9));
  Piano_1 piano_1_1 (
    .in_1(decoder_1_out2), .out_2(piano_1_1_out_2), .out_3(piano_1_1_out_3), .out_4(piano_1_1_out_4),
    .out_5(piano_1_1_out_5), .out_6(piano_1_1_out_6), .out_7(piano_1_1_out_7), .out_8(piano_1_1_out_8),
    .out_9(piano_1_1_out_9));
  Piano_terra piano_terra_1 (
    .in_1(decoder_1_out1), .out_2(piano_terra_1_out_2), .out_3(piano_terra_1_out_3),
    .out_4(piano_terra_1_out_4), .out_5(piano_terra_1_out_5), .out_6(piano_terra_1_out_6),
    .out_7(piano_terra_1_out_7), .out_8(piano_terra_1_out_8), .out_9(piano_terra_1_out_9));
  DotMatrix #(.matrixcols(24), .persist(1)) dotmatrix_8 (
    .col0(multiplexer_1_out), .col1(multiplexer_1_out), .col2(multiplexer_1_out), .col3(multiplexer_1_out),
    .col4(multiplexer_1_out), .col5(multiplexer_1_out), .col6(multiplexer_1_out), .col7(multiplexer_1_out),
    .col8(multiplexer_1_out), .col9(multiplexer_1_out), .col10(multiplexer_1_out), .col11(multiplexer_1_out),
    .col12(multiplexer_1_out), .col13(multiplexer_1_out), .col14(multiplexer_1_out),
    .col15(multiplexer_1_out), .col16(multiplexer_1_out), .col17(multiplexer_1_out),
    .col18(multiplexer_1_out), .col19(multiplexer_1_out), .col20(multiplexer_1_out),
    .col21(multiplexer_1_out), .col22(multiplexer_1_out), .col23(multiplexer_1_out));
  Multiplexer #(.select(2), .width(7)) multiplexer_1 (
    .in0(piano_terra_1_out_9), .in1(piano_1_1_out_9), .in2(piano_2_1_out_9), .in3(piano_3_1_out_9),
    .out(multiplexer_1_out), .sel(counter_3_q), .en(ON));

  // Notes on the sheet:
  //   on/off
  //   Scelta del piano
  //   <<< Numero di persone a bordo
  //   Con l'allarme attivo, nessuno sale o scende
  //   In caso di sovraccarico, la macchina si mette in pausa
  //   Output piano
  //   Posizione 
endmodule

module N_persone (
  input  [2:0] N_persone_input,
  output Errore
);

  wire decoder_1_out5, decoder_1_out6, decoder_1_out7;
  wire [3:0] decoder_1_out1;

  Decoder #(.select(3)) decoder_1 (
    .out1(decoder_1_out1[0]), .out2(decoder_1_out1[1]), .out3(decoder_1_out1[2]), .out4(decoder_1_out1[3]),
    .out5(decoder_1_out5), .out6(decoder_1_out6), .out7(decoder_1_out7), .sel(N_persone_input));  // open: out0, en
  or or_1 (Errore, decoder_1_out7, decoder_1_out6, decoder_1_out5);
  Hex_Digit_Display hex_digit_display_1 (.value(decoder_1_out1));  // open: dp
endmodule

module Errore_limite_superato (
  input  in_1,
  output [6:0] out_2,
  output [6:0] out_3,
  output [6:0] out_4,
  output [6:0] out_5,
  output [6:0] out_6,
  output [6:0] out_7,
  output [6:0] out_8,
  output [6:0] out_9,
  output [6:0] out_10,
  output [6:0] out_11,
  output [6:0] out_12,
  output [6:0] out_13,
  output [6:0] out_14,
  output [6:0] out_15,
  output [6:0] out_16,
  output [6:0] out_17,
  output [6:0] out_18,
  output [6:0] out_19,
  output [6:0] out_20,
  output [6:0] out_21,
  output [6:0] out_22
);

  Multiplexer #(.width(7)) multiplexer_1 (.in0({7{1'b0}}), .in1({7{1'b1}}), .out(out_2), .sel(in_1));  // open: en
  Multiplexer #(.width(7)) multiplexer_2 (.in0({7{1'b0}}), .in1(7'b1001001), .out(out_3), .sel(in_1));  // open: en
  Multiplexer #(.width(7)) multiplexer_3 (.in0({7{1'b0}}), .in1(7'b1001001), .out(out_4), .sel(in_1));  // open: en
  Multiplexer #(.width(7)) multiplexer_4 (.in0({7{1'b0}}), .in1(7'b1001001), .out(out_5), .sel(in_1));  // open: en
  Multiplexer #(.width(7)) multiplexer_5 (.in0({7{1'b0}}), .in1({7{1'b0}}), .out(out_6), .sel(in_1));  // open: en
  Multiplexer #(.width(7)) multiplexer_6 (.in0({7{1'b0}}), .in1({7{1'b0}}), .out(out_7), .sel(in_1));  // open: en
  Multiplexer #(.width(7)) multiplexer_7 (.in0({7{1'b0}}), .in1({7{1'b0}}), .out(out_8), .sel(in_1));  // open: en
  Multiplexer #(.width(7)) multiplexer_8 (.in0({7{1'b0}}), .in1({7{1'b1}}), .out(out_9), .sel(in_1));  // open: en
  Multiplexer #(.width(7)) multiplexer_9 (.in0({7{1'b0}}), .in1(7'b1011000), .out(out_10), .sel(in_1));  // open: en
  Multiplexer #(.width(7)) multiplexer_10 (.in0({7{1'b0}}), .in1(7'b1010100), .out(out_11), .sel(in_1));  // open: en
  Multiplexer #(.width(7)) multiplexer_11 (.in0({7{1'b0}}), .in1(7'b1110010), .out(out_12), .sel(in_1));  // open: en
  Multiplexer #(.width(7)) multiplexer_12 (.in0({7{1'b0}}), .in1(7'b0000001), .out(out_13), .sel(in_1));  // open: en
  Multiplexer #(.width(7)) multiplexer_13 (.in0({7{1'b0}}), .in1({7{1'b0}}), .out(out_14), .sel(in_1));  // open: en
  Multiplexer #(.width(7)) multiplexer_14 (.in0({7{1'b0}}), .in1({7{1'b0}}), .out(out_15), .sel(in_1));  // open: en
  Multiplexer #(.width(7)) multiplexer_15 (.in0({7{1'b0}}), .in1({7{1'b1}}), .out(out_16), .sel(in_1));  // open: en
  Multiplexer #(.width(7)) multiplexer_16 (.in0({7{1'b0}}), .in1(7'b1011000), .out(out_17), .sel(in_1));  // open: en
  Multiplexer #(.width(7)) multiplexer_17 (.in0({7{1'b0}}), .in1(7'b1010100), .out(out_18), .sel(in_1));  // open: en
  Multiplexer #(.width(7)) multiplexer_18 (.in0({7{1'b0}}), .in1(7'b1110010), .out(out_19), .sel(in_1));  // open: en
  Multiplexer #(.width(7)) multiplexer_19 (.in0({7{1'b0}}), .in1(7'b0000001), .out(out_20), .sel(in_1));  // open: en
  Multiplexer #(.width(7)) multiplexer_20 (.in0({7{1'b0}}), .in1({7{1'b0}}), .out(out_21), .sel(in_1));  // open: en
  Multiplexer #(.width(7)) multiplexer_21 (.in0({7{1'b0}}), .in1({7{1'b0}}), .out(out_22), .sel(in_1));  // open: en

  // Notes on the sheet:
  //   <<< Lettera E
  //   Lettera R>>>
  //   Lettera R>>>
endmodule
