// Logisim project es1_somma_e_differenza.circ as structural Verilog: 1 circuit, main circuit 4-bit Adder/Subtractor
module _4_bit_Adder_Subtractor (
  input  [3:0] B,
  input  [3:0] A,
  input  in_3,
  output [3:0] out_4,
  output out_5
);

  wire [3:0] xor_1_out;

  Adder #(.width(4)) adder_1 (.a(xor_1_out), .b(A), .out(out_4), .cin(in_3), .cout(out_5));
  xor xor_1 (xor_1_out[0], in_3, B[0]);
  xor xor_2 (xor_1_out[1], in_3, B[1]);
  xor xor_3 (xor_1_out[2], in_3, B[2]);
  xor xor_4 (xor_1_out[3], in_3, B[3]);
endmodule
