// Logisim project es2_circuito_overflow.circ as structural Verilog: 1 circuit, main circuit main
module main (
  input  a_n_1,
  input  s_n_1,
  input  b_n_1,
  output overflow
);

  wire xor_1_out, xor_2_out;

  xor xor_1 (xor_1_out, a_n_1, s_n_1);
  xor xor_2 (xor_2_out, s_n_1, b_n_1);
  and and_1 (overflow, xor_1_out, xor_2_out);
endmodule
