// Logisim project fulladder_con_halfadder.circ as structural Verilog: 2 circuits, main circuit Half adder
module Half_adder (
  input  A,
  input  B,
  output R,
  output S
);

  xor xor_1 (S, A, B);
  and and_1 (R, A, B);
endmodule

module Full_adder (
  input  A,
  input  B,
  input  R_IN,
  output R_OUT,
  output S
);

  wire half_adder_1_r, half_adder_1_s, half_adder_2_r;

  Half_adder half_adder_1 (.R(half_adder_1_r), .A(A), .B(B), .S(half_adder_1_s));
  Half_adder half_adder_2 (.R(half_adder_2_r), .A(half_adder_1_s), .B(R_IN), .S(S));
  or or_1 (R_OUT, half_adder_1_r, half_adder_2_r);
endmodule
