// Logisim project moltiplicatore_4bit.circ as structural Verilog: 1 circuit, main circuit 4-bit Multiplier
module _4_bit_Multiplier (
  input  A0,
  input  A1,
  input  A2,
  input  A3,
  input  B0,
  input  B1,
  input  B2,
  input  B3,
  output S0,
  output S1,
  output S2,
  output S3,
  output S4,
  output S5,
  output S6,
  output S7
);

  wire adder_1_cout, adder_2_cout, adder_2_out, adder_3_cout, adder_3_out, adder_4_cout, adder_4_out,
       adder_5_cout, adder_6_cout, adder_6_out, adder_7_cout, and_2_out, and_3_out, and_4_out, and_5_out,
       and_6_out, and_7_out, and_8_out, and_9_out, and_10_out, and_11_out, and_12_out, and_13_out,
       and_14_out, and_15_out, and_16_out, half_adder_1_r, half_adder_1_s, half_adder_2_r, half_adder_2_s,
       half_adder_3_s, half_adder_4_s;

  and and_1 (S0, A0, B0);
  and and_2 (and_2_out, A1, B0);
  and and_3 (and_3_out, A2, B0);
  and and_4 (and_4_out, A3, B0);
  and and_5 (and_5_out, A0, B1);
  and and_6 (and_6_out, A1, B1);
  and and_7 (and_7_out, A2, B1);
  and and_8 (and_8_out, A3, B1);
  and and_9 (and_9_out, A0, B2);
  and and_10 (and_10_out, A1, B2);
  and and_11 (and_11_out, A2, B2);
  and and_12 (and_12_out, A3, B2);
  and and_13 (and_13_out, A0, B3);
  and and_14 (and_14_out, A1, B3);
  and and_15 (and_15_out, A2, B3);
  and and_16 (and_16_out, A3, B3);
  Half_adder half_adder_1 (.R(half_adder_1_r), .A(and_9_out), .B(and_6_out), .S(half_adder_1_s));
  Half_adder half_adder_2 (.R(half_adder_2_r), .A(and_13_out), .B(and_10_out), .S(half_adder_2_s));
  Half_adder half_adder_3 (.R(S1), .A(and_5_out), .B(and_2_out), .S(half_adder_3_s));
  Adder #(.width(1)) adder_1 (.a(and_3_out), .b(half_adder_1_r), .out(S2), .cin(half_adder_3_s), .cout(adder_1_cout));
  Adder #(.width(1)) adder_2 (
    .a(half_adder_2_r), .b(and_7_out), .out(adder_2_out), .cin(half_adder_1_s), .cout(adder_2_cout));
  Adder #(.width(1)) adder_3 (
    .a(and_11_out), .b(and_14_out), .out(adder_3_out), .cin(half_adder_2_s), .cout(adder_3_cout));
  Adder #(.width(1)) adder_4 (
    .a(and_12_out), .b(and_15_out), .out(adder_4_out), .cin(adder_3_cout), .cout(adder_4_cout));
  Adder #(.width(1)) adder_5 (.a(adder_2_out), .b(and_4_out), .out(S3), .cin(adder_1_cout), .cout(adder_5_cout));
  Adder #(.width(1)) adder_6 (
    .a(and_8_out), .b(adder_3_out), .out(adder_6_out), .cin(adder_2_cout), .cout(adder_6_cout));
  Adder #(.width(1)) adder_7 (.a(adder_6_cout), .b(adder_4_out), .out(S5), .cin(half_adder_4_s), .cout(adder_7_cout));
  Adder #(.width(1)) adder_8 (.a(adder_4_cout), .b(and_16_out), .out(S6), .cin(adder_7_cout), .cout(S7));
  Half_adder half_adder_4 (.R(S4), .A(adder_6_out), .B(adder_5_cout), .S(half_adder_4_s));
endmodule
