// Logisim project Alu 1 bit.circ as structural Verilog: 1 circuit, main circuit main
module main (
  input  A,
  input  B,
  input  R_in,
  input  [2:0] S,
  input  Inverti_B,
  input  SET,
  output Risultato,
  output R_out,
  output OVERFLOW
);

  wire and_1_out, and_2_out, and_3_out, main_1_out_4, multiplexer_1_out, not_1_out, or_1_out;

  not not_1 (not_1_out, B);
  Multiplexer multiplexer_1 (.in0(B), .in1(not_1_out), .out(multiplexer_1_out), .sel(Inverti_B));  // open: en
  and and_1 (and_1_out, A, B);
  or or_1 (or_1_out, A, B);
  full_adder_main main_1 (.in_1(R_in), .in_2(A), .in_3(multiplexer_1_out), .out_4(main_1_out_4), .out_5(R_out));
  and and_2 (and_2_out, ~A, ~main_1_out_4, B);  // AND_Gate
  and and_3 (and_3_out, A, main_1_out_4, ~B);  // AND_Gate
  or or_2 (OVERFLOW, and_2_out, and_3_out);
  Multiplexer #(.select(3)) multiplexer_2 (
    .in0(and_1_out), .in1(or_1_out), .in2(main_1_out_4), .in3(SET), .in4(1'b0), .in5(1'b0), .in6(1'b0),
    .in7(1'b0), .out(Risultato), .sel(S));  // open: en
endmodule
