// Logisim project Decoder 4bit.circ as structural Verilog: 1 circuit, main circuit main
module main (
  input  B1,
  input  B2,
  input  B3,
  input  B4,
  output [14:0] out_5
);

  and and_1 (out_5[0], ~B1, ~B2, ~B3, ~B4);  // AND_Gate
  and and_2 (out_5[1], ~B1, ~B2, ~B3, B4);  // AND_Gate
  and and_3 (out_5[2], ~B1, ~B2, B3, ~B4);  // AND_Gate
  and and_4 (out_5[3], ~B1, B2, ~B3, ~B4);  // AND_Gate
  and and_5 (out_5[4], ~B1, B2, ~B3, B4);  // AND_Gate
  and and_6 (out_5[5], ~B1, B2, B3, ~B4);  // AND_Gate
  and and_7 (out_5[6], ~B1, B2, B3, B4);  // AND_Gate
  and and_8 (out_5[7], B1, ~B2, ~B3, ~B4);  // AND_Gate
  and and_9 (out_5[8], B1, ~B2, ~B3, B4);  // AND_Gate
  and and_10 (out_5[9], B1, ~B2, B3, ~B4);  // AND_Gate
  and and_11 (out_5[10], B1, ~B2, B3, B4);  // AND_Gate
  and and_12 (out_5[11], B1, B2, ~B3, ~B4);  // AND_Gate
  and and_13 (out_5[12], B1, B2, ~B3, B4);  // AND_Gate
  and and_14 (out_5[13], B1, B2, B3, ~B4);  // AND_Gate
  and and_15 (out_5[14], B1, B2, B3, B4);
endmodule
