// Logisim project Multiplexer a 16 vie.circ as structural Verilog: 2 circuits, main circuit Decoder 4 bit
module Decoder_4_bit (
  input  B1,
  input  B2,
  input  B3,
  input  B4,
  output [14:0] out_5
);

  and and_1 (out_5[0], ~B1, ~B2, ~B3, ~B4);  // AND_Gate
  and and_2 (out_5[1], ~B1, ~B2, ~B3, B4);  // AND_Gate
  and and_3 (out_5[2], ~B1, ~B2, B3, ~B4);  // AND_Gate
  and and_4 (out_5[3], ~B1, B2, ~B3, ~B4);  // AND_Gate
  and and_5 (out_5[4], ~B1, B2, ~B3, B4);  // AND_Gate
  and and_6 (out_5[5], ~B1, B2, B3, ~B4);  // AND_Gate
  and and_7 (out_5[6], ~B1, B2, B3, B4);  // AND_Gate
  and and_8 (out_5[7], B1, ~B2, ~B3, ~B4);  // AND_Gate
  and and_9 (out_5[8], B1, ~B2, ~B3, B4);  // AND_Gate
  and and_10 (out_5[9], B1, ~B2, B3, ~B4);  // AND_Gate
  and and_11 (out_5[10], B1, ~B2, B3, B4);  // AND_Gate
  and and_12 (out_5[11], B1, B2, ~B3, ~B4);  // AND_Gate
  and and_13 (out_5[12], B1, B2, ~B3, B4);  // AND_Gate
  and and_14 (out_5[13], B1, B2, B3, ~B4);  // AND_Gate
  and and_15 (out_5[14], B1, B2, B3, B4);
endmodule

module Multiplexer_a_16_vie (
  input  [14:0] in_1,
  input  [3:0] in_2,
  output out_3
);

  wire and_1_out, and_2_out, and_3_out, and_4_out, and_5_out, and_6_out, and_7_out, and_8_out, and_9_out,
       and_10_out, and_11_out, and_12_out, and_13_out, and_14_out, and_15_out;
  wire [14:0] decoder_4_bit_1_out_5;

  Decoder_4_bit decoder_4_bit_1 (.B1(in_2[0]), .B2(in_2[1]), .B3(in_2[2]), .B4(in_2[3]), .out_5(decoder_4_bit_1_out_5));
  and and_1 (and_1_out, in_1[0], decoder_4_bit_1_out_5[0]);
  and and_2 (and_2_out, in_1[1], decoder_4_bit_1_out_5[1]);
  and and_3 (and_3_out, in_1[2], decoder_4_bit_1_out_5[2]);
  and and_4 (and_4_out, in_1[3], decoder_4_bit_1_out_5[3]);
  and and_5 (and_5_out, in_1[4], decoder_4_bit_1_out_5[4]);
  and and_6 (and_6_out, in_1[5], decoder_4_bit_1_out_5[5]);
  and and_7 (and_7_out, in_1[6], decoder_4_bit_1_out_5[6]);
  and and_8 (and_8_out, in_1[7], decoder_4_bit_1_out_5[7]);
  and and_9 (and_9_out, in_1[8], decoder_4_bit_1_out_5[8]);
  and and_10 (and_10_out, in_1[9], decoder_4_bit_1_out_5[9]);
  and and_11 (and_11_out, in_1[10], decoder_4_bit_1_out_5[10]);
  and and_12 (and_12_out, in_1[11], decoder_4_bit_1_out_5[11]);
  and and_13 (and_13_out, in_1[12], decoder_4_bit_1_out_5[12]);
  and and_14 (and_14_out, in_1[13], decoder_4_bit_1_out_5[13]);
  and and_15 (and_15_out, in_1[14], decoder_4_bit_1_out_5[14]);
  or or_1 (out_3, and_1_out, and_2_out, and_3_out, and_4_out, and_5_out, and_6_out, and_7_out, and_8_out, and_9_out, and_10_out, and_11_out, and_12_out, and_13_out, and_14_out, and_15_out);
endmodule
