// Logisim project Nand porta universale.circ as structural Verilog: 1 circuit, main circuit main
module main (
  input  in_1,
  input  in_2,
  input  in_3,
  input  in_4,
  input  in_5,
  input  in_6,
  input  in_7,
  input  in_8,
  input  in_9,
  input  in_10,
  output AND,
  output out_12,
  output XNOR,
  output OR,
  output out_15
);

  wire nand_1_out, nand_2_out, nand_3_out, nand_4_out, nand_5_out, nand_6_out, nand_7_out, nand_9_out,
       nand_10_out, nand_11_out, nand_12_out, nand_14_out, nand_17_out;

  nand nand_1 (nand_1_out, in_5, in_6);
  nand nand_2 (nand_2_out, in_7, in_7);
  nand nand_3 (nand_3_out, in_8, in_8);
  nand nand_4 (nand_4_out, in_9, in_9);
  nand nand_5 (nand_5_out, in_10, in_10);
  nand nand_6 (nand_6_out, in_1, in_2);
  nand nand_7 (nand_7_out, in_3, in_4);
  nand nand_8 (AND, nand_6_out, nand_6_out);
  nand nand_9 (nand_9_out, nand_7_out, in_3);
  nand nand_10 (nand_10_out, nand_7_out, in_4);
  nand nand_11 (nand_11_out, nand_1_out, in_5);
  nand nand_12 (nand_12_out, nand_1_out, in_6);
  nand nand_13 (OR, nand_2_out, nand_3_out);
  nand nand_14 (nand_14_out, nand_4_out, nand_5_out);
  nand nand_15 (out_15, nand_14_out, nand_14_out);
  nand nand_16 (out_12, nand_9_out, nand_10_out);
  nand nand_17 (nand_17_out, nand_11_out, nand_12_out);
  nand nand_18 (XNOR, nand_17_out, nand_17_out);

  // Notes on the sheet:
  //   NOR
  //   XOR
endmodule
