// Logisim project moltiplicazione 2 bit.circ as structural Verilog: 1 circuit, main circuit main
module main (
  input  [1:0] a,
  input  [1:0] b,
  output [3:0] out_3
);

  wire a0b1_out, a1b0_out, a1b1_out, main_1_out_4;

  and a0b0 (out_3[0], a[0], b[0]);
  and a0b1 (a0b1_out, a[0], b[1]);
  and a1b0 (a1b0_out, a[1], b[0], b[0]);
  and a1b1 (a1b1_out, a[1], b[1]);
  half_adder_main main_1 (.in_1(a0b1_out), .in_2(a1b0_out), .out_3(out_3[1]), .out_4(main_1_out_4));
  half_adder_main main_2 (.in_1(a1b1_out), .in_2(main_1_out_4), .out_3(out_3[2]), .out_4(out_3[3]));
endmodule
