// Logisim project moltiplicazione a 4 bit- non funge.circ as structural Verilog: 1 circuit, main circuit main
module main (
  input  [3:0] A,
  input  [3:0] B,
  output [7:0] out_3
);

  wire a0b2_out, a0b3_out, a1b0_out, a1b1_out, a1b2_out, a1b3_out, a2b0_out, a2b1_out, a2b2_out, a2b3_out,
       a3b0_out, a3b1_out, a3b2_out, a3b3_out, main_2_out_4, main_2_out_5, main_3_out_5, main_4_out_3,
       main_4_out_4, main_5_out_4, main_5_out_5, main_6_out_5, main_7_out_4, main_7_out_5, main_8_out_4,
       main_8_out_5, main_9_out_4, main_10_out_4, main_10_out_5, main_11_out_4, main_12_out_4;

  and a0b0 (out_3[0], A[0], A[3]);
  // AND_Gate a0b1 has open pins: in0=A[0], in4=A[3], out=open
  and a0b2 (a0b2_out, A[0], A[3]);
  and a0b3 (a0b3_out, A[0], A[3]);
  and a1b0 (a1b0_out, A[1], A[3]);
  and a1b1 (a1b1_out, A[1], A[3]);
  and a1b2 (a1b2_out, A[1], A[3]);
  and a1b3 (a1b3_out, A[1], A[3]);
  and a2b0 (a2b0_out, A[2], A[3]);
  and a2b1 (a2b1_out, A[2], A[3]);
  and a2b2 (a2b2_out, A[2], A[3]);
  and a2b3 (a2b3_out, A[2], A[3]);
  and a3b0 (a3b0_out, A[3], A[3]);
  and a3b1 (a3b1_out, A[3], A[3]);
  and a3b2 (a3b2_out, A[3], A[3]);
  and a3b3 (a3b3_out, A[3], A[3]);
  full_adder_main main_1 (.in_1(main_2_out_5), .in_3(main_3_out_5), .out_4(out_3[6]), .out_5(out_3[7]));  // open: in_2
  full_adder_main main_2 (
    .in_1(main_4_out_4), .in_2(a3b0_out), .in_3(main_5_out_5), .out_4(main_2_out_4), .out_5(main_2_out_5));
  full_adder_main main_3 (
    .in_1(main_2_out_4), .in_2(a3b3_out), .in_3(main_6_out_5), .out_4(out_3[5]), .out_5(main_3_out_5));
  half_adder_main main_4 (.in_1(a2b0_out), .in_2(main_7_out_5), .out_3(main_4_out_3), .out_4(main_4_out_4));
  full_adder_main main_5 (
    .in_1(main_4_out_3), .in_2(a2b3_out), .in_3(main_8_out_5), .out_4(main_5_out_4), .out_5(main_5_out_5));
  full_adder_main main_6 (
    .in_1(main_5_out_4), .in_2(a3b2_out), .in_3(main_9_out_4), .out_4(out_3[4]), .out_5(main_6_out_5));
  full_adder_main main_7 (
    .in_1(a1b2_out), .in_2(a1b3_out), .in_3(main_10_out_5), .out_4(main_7_out_4), .out_5(main_7_out_5));
  full_adder_main main_8 (
    .in_1(main_7_out_4), .in_2(a2b2_out), .in_3(main_11_out_4), .out_4(main_8_out_4), .out_5(main_8_out_5));
  half_adder_main main_9 (.in_1(main_8_out_4), .in_2(a3b1_out), .out_3(out_3[3]), .out_4(main_9_out_4));
  full_adder_main main_10 (
    .in_1(a1b1_out), .in_2(a1b0_out), .in_3(main_12_out_4), .out_4(main_10_out_4), .out_5(main_10_out_5));
  half_adder_main main_11 (.in_1(main_10_out_4), .in_2(a2b1_out), .out_3(out_3[2]), .out_4(main_11_out_4));
  half_adder_main main_12 (.in_1(a0b2_out), .in_2(a0b3_out), .out_3(out_3[1]), .out_4(main_12_out_4));

  assign B = {4{A[3]}};
endmodule
