// Logisim project mux a 4 vie.circ as structural Verilog
module mux_a_4_vie (
  input  [3:0] in_1,
  input  in_2,
  input  in_3,
  output out_4
);

  wire and_1_out, and_2_out, and_3_out, and_4_out, main_1_out_3, main_1_out_4, main_1_out_5, main_1_out_6;

  decoder_2_bit_main main_1 (
    .in_1(in_2), .in_2(in_3), .out_3(main_1_out_3), .out_4(main_1_out_4), .out_5(main_1_out_5),
    .out_6(main_1_out_6));
  and and_1 (and_1_out, in_1[0], main_1_out_3);
  and and_2 (and_2_out, in_1[1], main_1_out_4);
  and and_3 (and_3_out, in_1[2], main_1_out_5);
  and and_4 (and_4_out, in_1[3], main_1_out_6);
  or or_1 (out_4, and_1_out, and_3_out, and_2_out, and_4_out);
endmodule
