// Logisim project sommatore 4 bit.circ as structural Verilog: 1 circuit, main circuit main
module main (
  input  [3:0] in_1,
  input  [3:0] in_2,
  output [4:0] out_3
);

  wire main_1_out_4, main_2_out_5, main_3_out_5;

  Hex_Digit_Display hex_digit_display_1 (.value(in_1));  // open: dp
  Hex_Digit_Display hex_digit_display_2 (.value(in_2));  // open: dp
  half_adder_main main_1 (.in_1(in_1[0]), .in_2(in_2[0]), .out_3(out_3[0]), .out_4(main_1_out_4));
  full_adder_main main_2 (.in_1(main_1_out_4), .in_2(in_1[1]), .in_3(in_2[1]), .out_4(out_3[1]), .out_5(main_2_out_5));
  full_adder_main main_3 (.in_1(main_2_out_5), .in_2(in_1[2]), .in_3(in_2[2]), .out_4(out_3[2]), .out_5(main_3_out_5));
  full_adder_main main_4 (.in_1(main_3_out_5), .in_2(in_1[3]), .in_3(in_2[3]), .out_4(out_3[3]), .out_5(out_3[4]));
  Hex_Digit_Display hex_digit_display_3 (.value(out_3[3:0]), .dp(out_3[4]));
endmodule
