// Logisim project sommatore a 8 bit.circ as structural Verilog: 1 circuit, main circuit main
module main (
  input  [7:0] A,
  input  [7:0] B,
  output [8:0] out_3
);

  wire main_1_out_4, main_2_out_5, main_3_out_5, main_4_out_5, main_5_out_5, main_6_out_5, main_7_out_5;

  half_adder_main main_1 (.in_1(A[0]), .in_2(B[0]), .out_3(out_3[0]), .out_4(main_1_out_4));
  full_adder_main main_2 (.in_1(A[1]), .in_2(B[1]), .in_3(main_1_out_4), .out_4(out_3[1]), .out_5(main_2_out_5));
  full_adder_main main_3 (.in_1(A[2]), .in_2(B[2]), .in_3(main_2_out_5), .out_4(out_3[2]), .out_5(main_3_out_5));
  full_adder_main main_4 (.in_1(A[3]), .in_2(B[3]), .in_3(main_3_out_5), .out_4(out_3[3]), .out_5(main_4_out_5));
  full_adder_main main_5 (.in_1(A[4]), .in_2(B[4]), .in_3(main_4_out_5), .out_4(out_3[4]), .out_5(main_5_out_5));
  full_adder_main main_6 (.in_1(A[5]), .in_2(B[5]), .in_3(main_5_out_5), .out_4(out_3[5]), .out_5(main_6_out_5));
  full_adder_main main_7 (.in_1(A[6]), .in_2(B[6]), .in_3(main_6_out_5), .out_4(out_3[6]), .out_5(main_7_out_5));
  full_adder_main main_8 (.in_1(A[7]), .in_2(B[7]), .in_3(main_7_out_5), .out_4(out_3[7]), .out_5(out_3[8]));
endmodule
